// Logisim project SAP1.circ as structural Verilog
module main (
  input  in_1,
  input  in_2,
  input  [7:0] Tester,
  input  [3:0] Address_Input,
  input  [7:0] _8_Bit_input,
  input  MAR_INPUT,
  input  in_7,
  input  Manual,
  input  in_9,
  input  in_10,
  input  in_11,
  input  in_12,
  input  in_13,
  input  in_14,
  input  in_15,
  input  in_16,
  input  in_17,
  input  in_18,
  input  in_19,
  input  in_20,
  input  in_21,
  input  in_22,
  input  in_23,
  input  in_24,
  output [7:0] Bus,
  output [3:0] Program_Counter,
  output [7:0] Accumulator,
  output [3:0] MAR,
  output [7:0] Adder,
  output [7:0] RAM,
  output [7:0] B,
  output [7:0] out_32,
  output [2:0] out_33
);

  wire AI, AO, BI, BO, CE, Clock_out, CO, H, II, IO, J, M, MI, not_1_out, OI, Pulse_out, RI, RO, SO;
  wire [3:0] n4_bit_register_1_out, Output_lsb, Output_msb, selector_1_out_6;
  wire [7:0] A_out, ALU_output, B_out, buffer_2_out, buffer_3_out, buffer_6_out, buffer_8_out, buffer_11_out,
       buffer_12_out, InstructionRegister_out, programcounter_1_out_2, selector_1_out_7;
  wire [15:0] control_logic_1_controlout;
  wire [31:0] Output_bcd;

  assign RI = Manual ? in_11 : 1'bz;  // Controlled_Buffer controlled_buffer_1
  assign RO = Manual ? in_12 : 1'bz;  // Controlled_Buffer controlled_buffer_2
  assign H = Manual ? in_9 : 1'bz;  // Controlled_Buffer controlled_buffer_3
  assign MI = Manual ? in_10 : 1'bz;  // Controlled_Buffer controlled_buffer_4
  assign AI = Manual ? in_15 : 1'bz;  // Controlled_Buffer controlled_buffer_5
  assign II = Manual ? in_14 : 1'bz;  // Controlled_Buffer controlled_buffer_6
  assign AO = Manual ? in_16 : 1'bz;  // Controlled_Buffer controlled_buffer_7
  assign IO = Manual ? in_13 : 1'bz;  // Controlled_Buffer controlled_buffer_8
  Selector selector_1 (
    .in_4(MAR_INPUT), .MAR4(n4_bit_register_1_out), .MAR8(Bus), .IN4(Address_Input), .IN8(_8_Bit_input),
    .out_6(selector_1_out_6), .out_7(selector_1_out_7), .out_8(selector_1_out_6), .out_9(selector_1_out_7));
  assign SO = Manual ? in_17 : 1'bz;  // Controlled_Buffer controlled_buffer_9
  assign M = Manual ? in_18 : 1'bz;  // Controlled_Buffer controlled_buffer_10
  assign BO = Manual ? in_20 : 1'bz;  // Controlled_Buffer controlled_buffer_11
  assign BI = Manual ? in_19 : 1'bz;  // Controlled_Buffer controlled_buffer_12
  ProgramCounter programcounter_1 (
    .Load(J), .in_2(buffer_2_out), .Increment(CE), .Out_2(programcounter_1_out_2), .Clock(Clock_out),
    .Out(CO), .out_6(Program_Counter));
  _4_bit_Register u_4_bit_register_1 (
    .In(buffer_3_out), .Load(MI), .Enable(1'b1), .State(MAR), .Out(n4_bit_register_1_out), .Clock(Clock_out));
  InstructionRegister InstructionRegister (
    .In(buffer_6_out), .Out(InstructionRegister_out), .L(II), .Clk(Clock_out), .En(IO), .out_5(out_32));
  Control_Logic control_logic_1 (.IR(out_32), .ControlOut(control_logic_1_controlout), .Clk(Clock_out), .Step(out_33));
  assign J = Manual ? in_24 : 1'bz;  // Controlled_Buffer controlled_buffer_13
  assign CO = Manual ? in_23 : 1'bz;  // Controlled_Buffer controlled_buffer_14
  assign CE = Manual ? in_22 : 1'bz;  // Controlled_Buffer controlled_buffer_15
  assign OI = Manual ? in_21 : 1'bz;  // Controlled_Buffer controlled_buffer_16
  assign Bus = programcounter_1_out_2;  // Buffer buffer_1, 8 bits wide
  assign buffer_2_out = Bus;  // Buffer buffer_2, 8 bits wide
  assign buffer_3_out = Bus;  // Buffer buffer_3, 8 bits wide
  assign Bus = RAM;  // Buffer buffer_4, 8 bits wide
  RAM #(.addrWidth(4), .bus("separate")) ram_1 (
    .addr(selector_1_out_6), .din(selector_1_out_7), .data(RAM), .str(RI), .clk(Clock_out), .ld(RO));  // open: sel, clr
  assign Bus = InstructionRegister_out;  // Buffer buffer_5, 8 bits wide
  assign buffer_6_out = Bus;  // Buffer buffer_6, 8 bits wide
  assign {H, MI, RI, RO, IO, II, AI, AO, SO, M, BI, BO, OI, CE, CO, J} = not_1_out ? control_logic_1_controlout : 16'bz;  // Controlled_Buffer controlled_buffer_17
  not not_1 (not_1_out, Manual);
  Pull_Resistor pull_resistor_1 (.node(Bus));
  assign Bus = in_2 ? Tester : 8'bz;  // Controlled_Buffer controlled_buffer_18
  assign Bus = A_out;  // Buffer buffer_7, 8 bits wide
  assign buffer_8_out = Bus;  // Buffer buffer_8, 8 bits wide
  assign Bus = ALU_output;  // Buffer buffer_9, 8 bits wide
  assign Bus = B_out;  // Buffer buffer_10, 8 bits wide
  assign buffer_11_out = Bus;  // Buffer buffer_11, 8 bits wide
  assign buffer_12_out = Bus;  // Buffer buffer_12, 8 bits wide
  _8_bit_Register A (.In(buffer_8_out), .Out(A_out), .Enable(AO), .Load(AI), .Clock(Clock_out), .State(Accumulator));
  ALU ALU (.A(Accumulator), .M(M), .Output(ALU_output), .B(B), .Enable(SO), .S(Adder));
  _8_bit_Register u_B (.In(buffer_11_out), .Out(B_out), .Enable(BO), .Load(BI), .Clock(Clock_out), .State(B));
  _8_bit_Display Output (
    .In(buffer_12_out), .BCD(Output_bcd), .LSB(Output_lsb), .MSB(Output_msb), .Enable(OI), .Clock(Clock_out),
    .Clear(in_7));
  Button Pulse (.out(Pulse_out));
  Clock Clock (.Pulse(Pulse_out), .Enable(in_1), .Out(Clock_out), .HLT(H));
  _7_Segment_Display u_7_segment_display_1 (
    .g(Output_bcd[19]), .f(Output_bcd[18]), .a(Output_bcd[17]), .b(Output_bcd[16]), .e(Output_bcd[23]),
    .d(Output_bcd[22]), .c(Output_bcd[21]), .dp(Output_bcd[20]));
  _7_Segment_Display u_7_segment_display_2 (
    .g(Output_bcd[27]), .f(Output_bcd[26]), .a(Output_bcd[25]), .b(Output_bcd[24]), .e(Output_bcd[31]),
    .d(Output_bcd[30]), .c(Output_bcd[29]), .dp(Output_bcd[28]));
  Hex_Digit_Display hex_digit_display_1 (.value(Output_msb));  // open: dp
  _7_Segment_Display u_7_segment_display_3 (
    .g(Output_bcd[3]), .f(Output_bcd[2]), .a(Output_bcd[1]), .b(Output_bcd[0]), .e(Output_bcd[7]),
    .d(Output_bcd[6]), .c(Output_bcd[5]), .dp(Output_bcd[4]));
  _7_Segment_Display u_7_segment_display_4 (
    .g(Output_bcd[11]), .f(Output_bcd[10]), .a(Output_bcd[9]), .b(Output_bcd[8]), .e(Output_bcd[15]),
    .d(Output_bcd[14]), .c(Output_bcd[13]), .dp(Output_bcd[12]));
  Hex_Digit_Display hex_digit_display_2 (.value(Output_lsb));  // open: dp

  // Notes on the sheet:
  //   Manual Control Edit
  //   SAP-I By Gil Emmanuel Bancud
  //   Control Signal Overview
  //   HEX
  //   BCD
endmodule

module ALU (
  input  Enable,
  input  [7:0] A,
  input  M,
  input  [7:0] B,
  output [7:0] Output,
  output [7:0] S
);

  wire [7:0] xor_1_out;

  assign xor_1_out = {8{M}} ^ B;  // XOR_Gate xor_1, 8 bits wide
  Adder adder_1 (.a(A), .b(xor_1_out), .out(S), .cin(M));  // open: cout
  assign Output = Enable ? S : 8'bz;  // Controlled_Buffer controlled_buffer_1
endmodule

module Clock (
  input  Pulse,
  input  Enable,
  input  HLT,
  output Out
);

  wire and_1_out, and_2_out, Clock_out, not_1_out, not_2_out, or_1_out;

  Clock_part Clock (.out(Clock_out));
  and and_1 (and_1_out, Clock_out, Enable);
  and and_2 (and_2_out, Pulse, not_1_out);
  not not_1 (not_1_out, Enable);
  or or_1 (or_1_out, and_1_out, and_2_out);
  assign Out = not_2_out ? or_1_out : 1'bz;  // Controlled_Buffer controlled_buffer_1
  Pull_Resistor pull_resistor_1 (.node(Out));
  not not_2 (not_2_out, HLT);
endmodule

module _8_bit_Register (
  input  [7:0] In,
  input  Clock,
  input  Load,
  input  Enable,
  output [7:0] State,
  output [7:0] Out
);

  wire [7:0] controlled_buffer_1_out;

  assign controlled_buffer_1_out = Load ? In : 8'bz;  // Controlled_Buffer controlled_buffer_1
  Register register_1 (.D(controlled_buffer_1_out), .Q(State), .clk(Clock));  // open: en, clr
  assign Out = Enable ? State : 8'bz;  // Controlled_Buffer controlled_buffer_2
endmodule

module _4_bit_Register (
  input  [7:0] In,
  input  Clock,
  input  Load,
  input  Enable,
  output [3:0] State,
  output [3:0] Out
);

  wire [3:0] bitselector_1_out, controlled_buffer_1_out;

  BitSelector #(.group(4)) bitselector_1 (.in(In), .out(bitselector_1_out), .sel(1'b0));
  assign controlled_buffer_1_out = Load ? bitselector_1_out : 4'bz;  // Controlled_Buffer controlled_buffer_1
  Register #(.width(4)) register_1 (.D(controlled_buffer_1_out), .Q(State), .clk(Clock));  // open: en, clr
  assign Out = Enable ? State : 4'bz;  // Controlled_Buffer controlled_buffer_2
endmodule

module Selector (
  input  [3:0] MAR4,
  input  [7:0] MAR8,
  input  [3:0] IN4,
  input  in_4,
  input  [7:0] IN8,
  output [3:0] out_6,
  output [7:0] out_7,
  output [3:0] out_8,
  output [7:0] out_9
);

  wire not_1_out;

  not not_1 (not_1_out, in_4);
  assign out_6 = not_1_out ? MAR4 : 4'bz;  // Controlled_Buffer _4
  assign out_7 = not_1_out ? MAR8 : 8'bz;  // Controlled_Buffer _8
  assign out_8 = in_4 ? IN4 : 4'bz;  // Controlled_Buffer _4_2
  assign out_9 = in_4 ? IN8 : 8'bz;  // Controlled_Buffer _8_2
endmodule

module ProgramCounter (
  input  Load,
  input  [7:0] in_2,
  input  Increment,
  input  Out,
  input  Clock,
  output [3:0] out_6,
  output [7:0] Out_2
);

  wire [3:0] bitselector_1_out;
  wire [7:0] bitselector_2_out;

  BitSelector #(.group(4)) bitselector_1 (.in(in_2), .out(bitselector_1_out), .sel(1'b0));
  Counter #(.width(4), .max('hf)) counter_1 (
    .load(Load), .D(bitselector_1_out), .count(Increment), .Q(out_6), .clk(Clock));  // open: carry, clr
  BitSelector #(.width(4), .group(8)) bitselector_2 (.in(out_6), .out(bitselector_2_out), .sel(1'b0));
  assign Out_2 = Out ? bitselector_2_out : 8'bz;  // Controlled_Buffer controlled_buffer_1
endmodule

module _8_bit_Display (
  input  [7:0] In,
  input  Enable,
  input  Clock,
  input  Clear,
  output [31:0] BCD,
  output [3:0] LSB,
  output [3:0] MSB
);

  wire [7:0] controlled_buffer_1_out, register_1_q;

  assign controlled_buffer_1_out = Enable ? In : 8'bz;  // Controlled_Buffer controlled_buffer_1
  Register register_1 (.D(controlled_buffer_1_out), .Q(register_1_q), .clk(Clock), .clr(Clear));  // open: en
  BitSelector #(.group(4)) bitselector_1 (.in(register_1_q), .out(LSB), .sel(1'b0));
  BitSelector #(.group(4)) bitselector_2 (.in(register_1_q), .out(MSB), .sel(1'b1));
  ROM #(.addrWidth(9), .dataWidth(32)) rom_1 (.addr({1'b1, register_1_q}), .data(BCD));  // open: sel

  // Notes on the sheet:
  //   contents of rom_1 (hex, n*v repeats v):
  //   e7 21 cb 6b 2d 6e ee 23 ef 6f 21e7 2121 21cb 216b 212d 216e 21ee 2123 21ef 216f cbe7 cb21 cbcb cb6b
  //   cb2d cb6e cbee cb23 cbef cb6f 6be7 6b21 6bcb 6b6b 6b2d 6b6e 6bee 6b23 6bef 6b6f 2de7 2d21 2dcb 2d6b
  //   2d2d 2d6e 2dee 2d23 2def 2d6f 6ee7 6e21 6ecb 6e6b 6e2d 6e6e 6eee 6e23 6eef 6e6f eee7 ee21 eecb ee6b
  //   ee2d ee6e eeee ee23 eeef ee6f 23e7 2321 23cb 236b 232d 236e 23ee 2323 23ef 236f efe7 ef21 efcb ef6b
  //   ef2d ef6e efee ef23 efef ef6f 6fe7 6f21 6fcb 6f6b 6f2d 6f6e 6fee 6f23 6fef 6f6f 21e7e7 21e721 21e7cb
  //   21e76b 21e72d 21e76e 21e7ee 21e723 21e7ef 21e76f 2121e7 212121 2121cb 21216b 21212d 21216e 2121ee
  //   212123 2121ef 21216f 21cbe7 21cb21 21cbcb 21cb6b 21cb2d 21cb6e 21cbee 21cb23 21cbef 21cb6f 216be7
  //   216b21 216bcb 216b6b 216b2d 216b6e 216bee 216b23 216bef 216b6f 212de7 212d21 212dcb 212d6b 212d2d
  //   212d6e 212dee 212d23 212def 212d6f 216ee7 216e21 216ecb 216e6b 216e2d 216e6e 216eee 216e23 216eef
  //   216e6f 21eee7 21ee21 21eecb 21ee6b 21ee2d 21ee6e 21eeee 21ee23 21eeef 21ee6f 2123e7 212321 2123cb
  //   21236b 21232d 21236e 2123ee 212323 2123ef 21236f 21efe7 21ef21 21efcb 21ef6b 21ef2d 21ef6e 21efee
  //   21ef23 21efef 21ef6f 216fe7 216f21 216fcb 216f6b 216f2d 216f6e 216fee 216f23 216fef 216f6f cbe7e7
  //   cbe721 cbe7cb cbe76b cbe72d cbe76e cbe7ee cbe723 cbe7ef cbe76f cb21e7 cb2121 cb21cb cb216b cb212d
  //   cb216e cb21ee cb2123 cb21ef cb216f cbcbe7 cbcb21 cbcbcb cbcb6b cbcb2d cbcb6e cbcbee cbcb23 cbcbef
  //   cbcb6f cb6be7 cb6b21 cb6bcb cb6b6b cb6b2d cb6b6e cb6bee cb6b23 cb6bef cb6b6f cb2de7 cb2d21 cb2dcb
  //   cb2d6b cb2d2d cb2d6e cb2dee cb2d23 cb2def cb2d6f cb6ee7 cb6e21 cb6ecb cb6e6b cb6e2d cb6e6e e7 21 cb
  //   6b 2d 6e ee 23 ef 6f 21e7 2121 21cb 216b 212d 216e 21ee 2123 21ef 216f cbe7 cb21 cbcb cb6b cb2d cb6e
  //   cbee cb23 cbef cb6f 6be7 6b21 6bcb 6b6b 6b2d 6b6e 6bee 6b23 6bef 6b6f 2de7 2d21 2dcb 2d6b 2d2d 2d6e
  //   2dee 2d23 2def 2d6f 6ee7 6e21 6ecb 6e6b 6e2d 6e6e 6eee 6e23 6eef 6e6f eee7 ee21 eecb ee6b ee2d ee6e
  //   eeee ee23 eeef ee6f 23e7 2321 23cb 236b 232d 236e 23ee 2323 23ef 236f efe7 ef21 efcb ef6b ef2d ef6e
  //   efee ef23 efef ef6f 6fe7 6f21 6fcb 6f6b 6f2d 6f6e 6fee 6f23 6fef 6f6f 21e7e7 21e721 21e7cb 21e76b
  //   21e72d 21e76e 21e7ee 21e723 21e7ef 21e76f 2121e7 212121 2121cb 21216b 21212d 21216e 2121ee 212123
  //   2121ef 21216f 21cbe7 21cb21 21cbcb 21cb6b 21cb2d 21cb6e 21cbee 21cb23 821cbef 821cb23 821cbee
  //   821cb6e 821cb2d 821cb6b 821cbcb 821cb21 821cbe7 821216f 82121ef 8212123 82121ee 821216e 821212d
  //   821216b 82121cb 8212121 82121e7 821e76f 821e7ef 821e723 821e7ee 821e76e 821e72d 821e76b 821e7cb
  //   821e721 821e7e7 8006f6f 8006fef 8006f23 8006fee 8006f6e 8006f2d 8006f6b 8006fcb 8006f21 8006fe7
  //   800ef6f 800efef 800ef23 800efee 800ef6e 800ef2d 800ef6b 800efcb 800ef21 800efe7 800236f 80023ef
  //   8002323 80023ee 800236e 800232d 800236b 80023cb 8002321 80023e7 800ee6f 800eeef 800ee23 800eeee
  //   800ee6e 800ee2d 800ee6b 800eecb 800ee21 800eee7 8006e6f 8006eef 8006e23 8006eee 8006e6e 8006e2d
  //   8006e6b 8006ecb 8006e21 8006ee7 8002d6f 8002def 8002d23 8002dee 8002d6e 8002d2d 8002d6b 8002dcb
  //   8002d21 8002de7 8006b6f 8006bef 8006b23 8006bee 8006b6e 8006b2d 8006b6b 8006bcb 8006b21 8006be7
  //   800cb6f 800cbef 800cb23 800cbee 800cb6e 800cb2d 800cb6b 800cbcb 800cb21 800cbe7 800216f 80021ef
  //   8002123 80021ee 800216e 800212d 800216b 80021cb 8002121 80021e7 800006f 80000ef 8000023 80000ee
  //   800006e 800002d 800006b 80000cb 8000021
endmodule

module InstructionRegister (
  input  [7:0] In,
  input  L,
  input  En,
  input  Clk,
  output [7:0] out_5,
  output [7:0] Out
);

  wire [3:0] bitselector_1_out;
  wire [7:0] bitselector_2_out, controlled_buffer_1_out;

  assign controlled_buffer_1_out = L ? In : 8'bz;  // Controlled_Buffer controlled_buffer_1
  Register register_1 (.D(controlled_buffer_1_out), .Q(out_5), .clk(Clk));  // open: en, clr
  BitSelector #(.group(4)) bitselector_1 (.in(out_5), .out(bitselector_1_out), .sel(1'b0));
  BitSelector #(.width(4), .group(8)) bitselector_2 (.in(bitselector_1_out), .out(bitselector_2_out), .sel(1'b0));
  assign Out = En ? bitselector_2_out : 8'bz;  // Controlled_Buffer controlled_buffer_2
endmodule

module Control_Logic (
  input  Clk,
  input  [7:0] IR,
  output [15:0] ControlOut,
  output [2:0] Step
);

  wire decoder_1_out0, decoder_1_out1, decoder_1_out2, decoder_1_out3, decoder_1_out4, decoder_1_out5,
       decoder_1_out6, decoder_1_out7, not_1_out;
  wire [3:0] bitselector_1_out;

  not not_1 (not_1_out, Clk);
  Decoder #(.select(3)) decoder_1 (
    .out0(decoder_1_out0), .out1(decoder_1_out1), .out2(decoder_1_out2), .out3(decoder_1_out3),
    .out4(decoder_1_out4), .out5(decoder_1_out5), .out6(decoder_1_out6), .out7(decoder_1_out7), .sel(Step),
    .en(1'b1));
  Counter #(.width(3), .max('h7)) counter_1 (
    .count(1'b1), .Q(Step), .clk(not_1_out), .clr(decoder_1_out6));  // open: load, D, carry
  BitSelector #(.group(4)) bitselector_1 (.in(IR), .out(bitselector_1_out), .sel(1'b1));
  ROM #(.addrWidth(7), .dataWidth(16)) rom_1 (.addr({bitselector_1_out, Step}), .data(ControlOut));  // open: sel

  // Notes on the sheet:
  //   contents of rom_1 (hex, n*v repeats v):
  //   4002 1404 6*0 4002 1404 4800 1200 4*0 4002 1404 4800 1020 280 0 0 0 4002 1404 6*0 4002 1404 6*0 4002
  //   1404 6*0 4002 1404 6*0 4002 1404 6*0 4002 1404 6*0 4002 1404 6*0 4002 1404 6*0 4002 1404 6*0 4002
  //   1404 6*0 4002 1404 6*0 4002 1404 108 5*0 4002 1404
endmodule

module InstructionSetProgrammer (
  input  [6:0] in_1,
  input  [7:0] in_2,
  input  [7:0] in_3
);

  wire button_1_out;

  Button button_1 (.out(button_1_out));
  RAM #(.addrWidth(7), .dataWidth(16), .bus("separate")) ram_1 (
    .addr(in_1), .din({in_2, in_3}), .str(button_1_out), .clk(button_1_out));  // open: data, sel, ld, clr
endmodule
